# Fritzing sketch Otomasi Conveyor (saved by Fritzing 0.9.3b)
breadboards: 1

parts:
  Part1 = Arduino Nano (Rev3.0)
  DRV_1 = DRV 8825 Stepper Motor Carrier, High Current [part_number="DRV 8825"]
  S1 = Momentary Switch [package=ksa_sealed_tac_switch]
  S3 = Momentary Switch [package=ksa_sealed_tac_switch]
  S4 = Momentary Switch [package=ksa_sealed_tac_switch]
  R2 = Resistor [tolerance=±5% resistance=220 package=THT]
  R3 = Resistor [tolerance=±5% resistance=220 package=THT]
  R4 = Resistor [tolerance=±5% resistance=220 package=THT]
  S5 = Toggle Switch [package=THT]
  H1 = polarizedheader 4pin 0.156in [package=THT]
  J1 = Screw terminal - 2 pins [package=THT]
  VCC1 = Battery
  M1 = E18-D80NK_1 [package=THT]
  LED1 = smd LED [color="Blue (430nm)" package="0805 [SMD]"]
  LED2 = smd LED [color="Green (555nm)" package="0805 [SMD]"]
  J2 = Basic Servo
  S6 = Momentary Switch [package=ksa_sealed_tac_switch]
  R5 = Resistor [tolerance=±5% resistance=220 package=THT]
  OLED_I2C1 = OLED 128x64 I2C Monochrome Display
  C2 = Capacitor Polarized [package=cpol-radial-10uf-25v]

nets:
  GND: Part1.GND, DRV_1.GROUND_LOG, R2.Pin_1, R3.Pin_1, R4.Pin_1, VCC1.-, M1.pin1, LED1.cathode, LED2.cathode, J2.gnd, R5.Pin_1, OLED_I2C1.GND
  N1: Part1.D2, LED2.anode
  N2: Part1.D3, LED1.anode
  N3: Part1.D6, S6.1, R5.Pin_0
  N4: Part1.D7, S1.1, R4.Pin_0
  N5: Part1.D8, S3.1, R3.Pin_0
  N6: Part1.D9, S4.1, R2.Pin_0
  N7: Part1.D10, DRV_1.STEP
  N8: Part1.D11/MOSI, DRV_1.DIRECTION
  N9: Part1.VIN, VCC1.+
  5V: Part1.5V, DRV_1.RESET, DRV_1.SLEEP, S1.3, S3.3, S4.3, M1.pin2, J2.vcc, S6.3, OLED_I2C1.VDD
  N10: Part1.A5, OLED_I2C1.SDA
  N11: Part1.A4, OLED_I2C1.SCK
  N12: Part1.A0, M1.pin3
  N13: Part1.D13/SCK, J2.pulse
  N14: DRV_1.VOLTAGE_ST/_MT, S5.COM, C2.+
  N15: DRV_1.GROUND_ST/_MT, J1.pin2, C2.-
  N16: DRV_1.OUT_2B, H1.pin1
  N17: DRV_1.OUT_2A, H1.pin2
  N18: DRV_1.OUT_1A, H1.pin3
  N19: DRV_1.OUT_1B, H1.pin4
  N20: S5.L2, J1.pin1

custom parts:
  Battery: Your standard 2x 18650 battery pack (7,4 Volts)
  E18-D80NK_1: E18-D80NK Proximity Sensor module.
